# Fritzing sketch bebedero_test (saved by Fritzing 0.9.4)
breadboards: 1

parts:
  Part1 = Arduino Nano (Rev3.0)
  KY-1 = Keyes Relay [package=THT]
  M1 = DC Motor

nets:
  N1: Part1.GND, M1.pin_1
  N2: Part1.D7, KY-1.signal
  N3: KY-1.NO, M1.pin_2

notes:
  Common GND for all the elements. If different power rails are used, you have to connect them by a wire
  Yellow: red cable
  Green: black cable
  The relay model isn't this, but quite similar to mine (JQC-3FF-S-Z). At least, it does the same and look like my relay module.
  For the tests, I powered the arduino board with USB, and I always prefer not to power other components with 5V output of the Arduino board because it's safer (if one component requires a lot of current, for example, this way I won't damage Arduino)

custom parts:
  Keyes Relay: The Keyes 5V relay module is suitable for SCM development, home appliance control. It uses a 5V~12V TIL control signal which can control DC / AC signal.
