# Fritzing sketch Water_Tank_Level_Sensor (saved by Fritzing 0.9.6b)
circuit board: 3.7818cm x 2.82224cm
breadboards: 1

parts:
  U1 = ATTINY45 [package=dip]
  S1 = Square Pushbutton
  VCC1 = Battery block 9V
  J1 = female pin header, 4 pins [form="♀ (female)"]
  J3 = female pin header, 4 pins [form="♀ (female)"]
  J4 = female pin header, 2 pins [form="♀ (female)"]
  J5 = female pin header, 2 pins [form="♀ (female)"]
  R1 = Resistor [tolerance=±5% resistance=1k package=THT]
  R2 = Resistor [tolerance=±5% resistance=1k package=THT]
  R3 = Resistor [tolerance=±5% resistance=220 package=THT]
  R4 = Resistor [tolerance=±5% resistance=220 package=THT]
  LED1 = LED - 5mm [color="Red (633nm)" package="5 mm [THT]"]
  LED2 = LED - 5mm [color="Red (633nm)" package="5 mm [THT]"]
  IC1 = Voltage Regulator [package=to-220-alt]
  C1 = Electrolytic Capacitor [capacitance=100µF package="100 mil [THT, electrolytic]"]
  C2 = Electrolytic Capacitor [capacitance=100µF package="100 mil [THT, electrolytic]"]

nets:
  N1: U1.PB5(NRES), J3.pin1
  N2: U1.PB3(ADC3), J3.pin2, J5.pin1, R1.Pin_1
  N3: U1.PB4(ADC2), J3.pin3, J5.pin2, R2.Pin_1
  GND: U1.GND, VCC1.-, J3.pin4, R1.Pin_0, R2.Pin_0, LED1.cathode, LED2.cathode, IC1.GND, C1.-, C2.-
  N4: U1.PB0(MOSI), J1.pin4, R4.Pin_1
  N5: U1.PB1(MISO), J1.pin3, R3.Pin_1
  N6: U1.PB2(SCK_ADC1), J1.pin2
  N7: U1.VCC, J1.pin1, J4.pin1, J4.pin2, IC1.OUT, C2.+
  N8: S1.leg0, VCC1.+
  N9: S1.leg1, IC1.IN, C1.+
  N10: R3.Pin_0, LED1.anode
  N11: R4.Pin_0, LED2.anode

notes:
  Level Sensor (c) vu2aeo
