# Fritzing sketch bebedero_test (saved by Fritzing 0.9.6b)
breadboards: 1

parts:
  Part1 = Arduino Nano (Rev3.0)
  KY-1 = Keyes Relay [package=THT]
  M1 = DC Motor
  S4 = Square Pushbutton
  S5 = Square Pushbutton
  R3 = Resistor [tolerance=±5% resistance=10k package=THT]
  YwRobot_Power_Supply1 = YwRobot Breadboard Power Supply [part_number=545043]
  LED1 = LED - 5mm [color="Red (633nm)" package="5 mm [THT]"]
  Q1 = NPN-Transistor [package="SOT-23 [SMD]"]
  R4 = Resistor [tolerance=±5% resistance=1k package=THT]
  R1 = Resistor [tolerance=±5% resistance=10k package=THT]

nets:
  GND: Part1.GND, M1.pin_1, S4.leg0, S5.leg0, YwRobot_Power_Supply1.GND, Q1.2
  N1: Part1.D7, R4.Pin_1
  N2: Part1.D8, S4.leg1, R3.Pin_1
  N3: Part1.D10, S5.leg1, R1.Pin_1
  N4: KY-1.signal, Q1.1
  N5: KY-1.NO, M1.pin_2
  N6: R3.Pin_0, YwRobot_Power_Supply1.VCC#5, R1.Pin_0
  N7: LED1.cathode, Q1.0
  N8: LED1.anode, R4.Pin_0

notes:
  Common GND for all the elements. If different power rails are used, you have to connect them by a wire
  Yellow: red cable (+5V)
  Green: black cable (GND)
  The relay model isn't this, but quite similar to mine (JQC-3FF-S-Z). At least, it does the same and look like my relay module.
  For the tests, I powered the arduino board with USB, and I always prefer not to power other components with 5V output of the Arduino board because it's safer (if one component requires a lot of current, for example, this way I won't damage Arduino)
  Connections:
  D7 -- 1kohm resistor -- LED anode -- LED cathode -- base pin of 2N2222
  Collector pin of 2N2222 -- input relay pin
  Emitter pin of 2N2222 -- GND
  Water level switches:
  Switch 1: D8 -- pull-down resistor between D8 pin and switch
  Switch 2: Same way for D10

custom parts:
  Keyes Relay: The Keyes 5V relay module is suitable for SCM development, home appliance control. It uses a 5V~12V TIL control signal which can control DC / AC signal.
  YwRobot Breadboard Power Supply: The YwRobot Breadboard Power Supply (MB-V2) has two power rails; they can be 5V or 3V3. Power to the module can be provided through the female USB socket or through the A10 (female) 2.1mm power jack.
